# Fritzing sketch COEUR FRITZING (saved by Fritzing 0.9.3b)
breadboards: 1

parts:
  LED8 = LED - 5mm [color="Red (633nm)" package="5 mm [THT]"]
  part = LED - 5mm [color="Red (633nm)" package="5 mm [THT]"]
  LED2 = LED - 5mm [color="Red (633nm)" package="5 mm [THT]"]
  R5 = Resistor [tolerance=±5% resistance=220 package=THT]
  R3 = Resistor [tolerance=±5% resistance=220 package=THT]
  LED4 = LED - 5mm [color="Red (633nm)" package="5 mm [THT]"]
  R1 = Resistor [tolerance=±5% resistance=220 package=THT]
  LED10 = LED - 5mm [color="Red (633nm)" package="5 mm [THT]"]
  Composant1 = Arduino Uno (Rev3)
  R2 = Resistor [tolerance=±5% resistance=220 package=THT]
  R6 = Resistor [tolerance=±5% resistance=220 package=THT]
  R7 = Resistor [tolerance=±5% resistance=220 package=THT]
  LED13 = LED - 5mm [color="Red (633nm)" package="5 mm [THT]"]
  LED12 = LED - 5mm [color="Red (633nm)" package="5 mm [THT]"]
  R9 = Resistor [tolerance=±5% resistance=220 package=THT]
  LED11 = LED - 5mm [color="Red (633nm)" package="5 mm [THT]"]
  LED5 = LED - 5mm [color="Red (633nm)" package="5 mm [THT]"]
  R8 = Resistor [tolerance=±5% resistance=220 package=THT]
  R10 = Resistor [tolerance=±5% resistance=220 package=THT]
  R4 = Resistor [tolerance=±5% resistance=220 package=THT]
  LED1 = LED - 5mm [color="Red (633nm)" package="5 mm [THT]"]

nets (from the schematic view):
  N1: LED8.cathode, Composant1.D5_PWM
  N2: LED8.anode, R7.Pin_0
  N3: part.cathode, Composant1.D3_PWM
  N4: part.anode, R2.Pin_1
  N5: LED2.cathode, Composant1.D4
  N6: LED2.anode, R5.Pin_0, R9.Pin_1
  N7: R5.Pin_1, Composant1.GND, R10.Pin_1
  N8: R3.Pin_0, R9.Pin_0
  N9: R3.Pin_1, LED4.anode, LED13.anode, LED12.anode, R10.Pin_0
  N10: LED4.cathode, Composant1.D10_PWM/SS
  N11: R1.Pin_1, LED10.anode
  N12: LED10.cathode, Composant1.D6_PWM
  N13: Composant1.D8, LED1.cathode
  N14: Composant1.D9_PWM, LED13.cathode
  N15: Composant1.D12/MISO, LED12.cathode
  N16: Composant1.D2, LED11.cathode
  N17: Composant1.D7, LED5.cathode
  N18: R6.Pin_1, LED1.anode
  N19: LED11.anode, R8.Pin_1
  N20: LED5.anode, R4.Pin_0
