# Fritzing sketch cardio fréq (saved by Fritzing 0.9.3b)
breadboards: 1

parts:
  Composant1 = Arduino Uno (Rev3) - ICSP
  U1 = LM124-324 Quad Opamp [part_number=LM324N package="DIP (Dual Inline)"]
  R1 = Resistor [tolerance=±5% resistance=2.2k package=THT]
  R2 = Resistor [tolerance=±5% resistance=22k package=THT]
  R3 = Resistor [tolerance=±5% resistance=68k package=THT]
  R4 = Resistor [tolerance=±5% resistance=1k package=THT]
  R5 = Resistor [tolerance=±5% resistance=470k package=THT]
  R6 = Resistor [tolerance=±5% resistance=100 package=THT]
  LED1 = LED - 5mm [color="Red (633nm)" package="5 mm [THT]"]
  R7 = PHOTOCELL [package=photocell-kit]
  C1 = Ceramic Capacitor [capacitance=1µF package="100 mil [THT, multilayer]"]  # not connected
  C2 = Ceramic Capacitor [capacitance=100nF package="100 mil [THT, multilayer]"]
  LED3 = LED - 5mm [color="Red (633nm)" package="5 mm [THT]"]  # not connected

nets (from the schematic view):
  N1: Composant1.A0, R6.Pin_1
  N2: Composant1.5V, U1.VCC+, R1.Pin_0, R2.Pin_0
  N3: Composant1.GND, U1.VCC-
  N4: U1.2IN+, R3.Pin_1
  N5: U1.2IN-, R4.Pin_1, R5.Pin_0, C2.1
  N6: U1.2OUT, R5.Pin_1, R6.Pin_0, C2.0
  N7: R1.Pin_1, LED1.anode
  N8: R2.Pin_1, R7.P$1
  N9: R3.Pin_0, R4.Pin_0, LED1.cathode, R7.P$2
